# Fritzing sketch RoomSensor (saved by Fritzing 0.9.10b)
breadboards: 1

parts:
  WeMos_D1_Mini1 = WeMos D1 Mini
  BMP280_1 = BME280 Breakout
  BMP280_2 = BME280 Breakout
  R1 = Resistor [tolerance=±5% resistance=4.7k package="0402 [SMD]"]
  R2 = PHOTOCELL [package=photocell]

nets:
  3.3V: WeMos_D1_Mini1.3V3, BMP280_1.3.3V, BMP280_2.3.3V
  N1: WeMos_D1_Mini1.5V, R2.P$1
  GND: WeMos_D1_Mini1.A0, BMP280_1.GND, BMP280_2.GND, R1.Pin_1, R2.P$2
  N2: WeMos_D1_Mini1.D0, WeMos_D1_Mini1.RST
  N3: WeMos_D1_Mini1.D1, BMP280_1.SCK/SCL, BMP280_2.SCK/SCL
  N4: WeMos_D1_Mini1.D2, BMP280_1.SDI/SDA, BMP280_2.SDI/SDA
  N5: WeMos_D1_Mini1.G, R1.Pin_0
